// Logisim project Avance Practica4.circ as structural Verilog
module main (
  input  C_in,
  input  A,
  input  B,
  output Suma,
  output Carry_Out
);

  wire and_1_out, and_2_out, xor_1_out;

  xor xor_1 (xor_1_out, A, B);
  and and_1 (and_1_out, A, B);
  xor xor_2 (Suma, C_in, xor_1_out);
  and and_2 (and_2_out, C_in, xor_1_out);
  or or_1 (Carry_Out, and_2_out, and_1_out);

  // Notes on the sheet:
  //   Full Adder Ejercicio 1
endmodule

module Ejercicio_2 (
  input  [7:0] in_1,
  input  C,
  input  [7:0] in_3,
  output [7:0] out_4
);

  wire main_1_carry_out, main_2_carry_out, main_3_carry_out, main_4_carry_out, main_5_carry_out,
       main_6_carry_out, main_7_carry_out;

  main main_1 (.C_in(C), .A(in_1[0]), .B(in_3[0]), .Suma(out_4[0]), .Carry_Out(main_1_carry_out));
  main main_2 (.C_in(main_1_carry_out), .A(in_1[1]), .B(in_3[1]), .Suma(out_4[1]), .Carry_Out(main_2_carry_out));
  main main_3 (.C_in(main_2_carry_out), .A(in_1[2]), .B(in_3[2]), .Suma(out_4[2]), .Carry_Out(main_3_carry_out));
  main main_4 (.C_in(main_3_carry_out), .A(in_1[3]), .B(in_3[3]), .Suma(out_4[3]), .Carry_Out(main_4_carry_out));
  main main_5 (.C_in(main_4_carry_out), .A(in_1[4]), .B(in_3[4]), .Suma(out_4[4]), .Carry_Out(main_5_carry_out));
  main main_6 (.C_in(main_5_carry_out), .A(in_1[5]), .B(in_3[5]), .Suma(out_4[5]), .Carry_Out(main_6_carry_out));
  main main_7 (.C_in(main_6_carry_out), .A(in_1[6]), .B(in_3[6]), .Suma(out_4[6]), .Carry_Out(main_7_carry_out));
  main main_8 (.C_in(main_7_carry_out), .A(in_1[7]), .B(in_3[7]), .Suma(out_4[7]));  // open: Carry_Out

  // Notes on the sheet:
  //   A
  //   B
endmodule

module Ejercicio_4 (
  input  C_in,
  input  A,
  input  B,
  output Suma,
  output Carry_Out
);

  wire and_1_out, and_2_out, not_1_out, xor_1_out;

  not not_1 (not_1_out, A);
  xor xor_1 (xor_1_out, A, B);
  and and_1 (and_1_out, not_1_out, B);
  xor xor_2 (Suma, C_in, xor_1_out);
  and and_2 (and_2_out, C_in, xor_1_out);
  or or_1 (Carry_Out, and_2_out, and_1_out);
endmodule
